# Fritzing sketch LED_Array (saved by Fritzing 0.9.3b)
breadboards: 1

parts:
  LED2 = smd LED [color="Blue (470nm)" package="0603 [SMD]"]
  R2 = Resistor [tolerance=±5% resistance=220 package="2512 [SMD]"]
  Part1 = Ethernet Pro
  LED3 = smd LED [color="Green (560nm)" package="0805 [SMD]"]
  LED4 = smd LED [color="Red (633nm)" package="0805 [SMD]"]  # not connected
  LED5 = smd LED [color="Green (560nm)" package="0805 [SMD]"]
  LED6 = smd LED [color="Blue (470nm)" package="0805 [SMD]"]  # not connected
  R3 = Resistor [tolerance=±5% resistance=220 package="2512 [SMD]"]
  R4 = Resistor [tolerance=±5% resistance=220 package="2512 [SMD]"]
  R5 = Resistor [tolerance=±5% resistance=220 package="2512 [SMD]"]
  R6 = Resistor [tolerance=±5% resistance=220 package="2512 [SMD]"]
  R7 = Resistor [tolerance=±5% resistance=220 package="2512 [SMD]"]
  LED7 = smd LED [color="Red (633nm)" package="0805 [SMD]"]  # not connected

nets:
  N1: LED2.anode, Part1.GND, LED3.anode, LED5.anode
  N2: R2.Pin_0, Part1.IO3
  N3: Part1.IO2, R7.Pin_0
  N4: Part1.IO4, R3.Pin_0
  N5: Part1.IO5, R4.Pin_0
  N6: Part1.IO6, R5.Pin_0
  N7: Part1.IO7, R6.Pin_0
